# Fritzing sketch EFP_SCHEMATIC (saved by Fritzing 1.0.4)
breadboards: 1

parts:
  Part1 = Arduino Mega 2560 (Rev3)
  SP1 = SPEAKER [package=pcb_mount_speaker]
  C2 = Capacitor Polarized [package=cpol-radial-10uf-25v]
  M1 = PAM8403 Stereo Amplifier with Volume Control [part_number=HW-012]
  R1 = Rotary Potentiometer (Small) [maximum_resistance=10kΩ knob_status=50% power=0.5W package=THT]
  R2 = Resistor [tolerance=±5% resistance=220 package="2512 [SMD]"]
  R3 = Rotary Potentiometer (Small) [maximum_resistance=10kΩ knob_status=50% power=0.5W package=THT]
  R4 = Rotary Potentiometer (Small) [maximum_resistance=10kΩ knob_status=50% power=0.5W package=THT]
  R5 = Rotary Potentiometer (Small) [maximum_resistance=10kΩ knob_status=50% power=0.5W package=THT]
  R6 = Rotary Potentiometer (Small) [maximum_resistance=10kΩ knob_status=50% power=0.5W package=THT]

nets:
  N1: Part1.A0, R1.wiper
  N2: Part1.A1, R3.wiper
  N3: Part1.A2, R4.wiper
  N4: Part1.A3, R5.wiper
  N5: Part1.A4, R6.wiper
  N6: Part1.D11_PWM, R2.Pin_1
  N7: Part1.5V, M1.POWER+, R1.leg2, R3.leg2, R4.leg2, R5.leg2
  N8: Part1.GND, C2.+, M1.POWER-, M1.INPUTG, R1.leg1, R2.Pin_0, R3.leg1, R4.leg1, R5.leg1, R6.leg1
  N9: SP1.+, M1.LOUT-
  N10: SP1.-, M1.LOUT+
  N11: C2.-, M1.INPUTR

custom parts:
  PAM8403 Stereo Amplifier with Volume Control: PAM8403 stereo amplifier module with volume control Descriptive words Links: PAM8403 product datasheet
